# Fritzing sketch KRETSSCHEMA (saved by Fritzing 0.9.3b)
breadboards: 1

parts:
  ARDUINO_UNO = Arduino Uno (Rev3)
  SMS = Soil Moisture Sensor
  RIGHT = Pushbutton [package="[THT]"]
  LEFT = Pushbutton [package="[THT]"]
  LCD_16X2_I2C = 24LC04 [package=THT]
  WATERSNR = mystery part, 3 pins [chip_label=FUNDUINO]
  DHT11 = mystery part, 3 pins [chip_label=DHT11]
  PHOTOTRANSISTOR = mystery part, 3 pins [chip_label=PHOTO]
  R1 = Resistor [tolerance=±5% resistance=10k package=THT]
  R2 = Resistor [tolerance=±5% resistance=10k package=THT]
  DS3231 = Real Time Clock Module - DS1307 RTC Breakout Board
  LED_WARNING = LED - 5mm [color="Yellow (595nm)" package="5 mm [THT]"]
  LED_CRITICAL = LED - 5mm [color="Red (633nm)" package="5 mm [THT]"]
  R3 = Resistor [tolerance=±5% resistance=330 package=THT]
  R4 = Resistor [tolerance=±5% resistance=330 package=THT]
  DHT11_modul = mystery part, 3 pins [chip_label=DHT11]

nets (from the schematic view):
  N1: ARDUINO_UNO.A0, PHOTOTRANSISTOR.pin1
  N2: ARDUINO_UNO.A1, WATERSNR.pin3
  N3: ARDUINO_UNO.A2, SMS.SIG
  N4: ARDUINO_UNO.A5/SCL, LCD_16X2_I2C.SCL_-_I2C_Clock, DS3231.SCL
  N5: ARDUINO_UNO.D8, DHT11.pin2
  N6: ARDUINO_UNO.D11_PWM/MOSI, LEFT.Pin_4, R1.Pin_1
  N7: ARDUINO_UNO.D12/MISO, RIGHT.Pin_4, R2.Pin_1
  GND: ARDUINO_UNO.GND, SMS.GND, RIGHT.Pin_2, LEFT.Pin_2, LCD_16X2_I2C.0V, WATERSNR.pin1, DHT11.pin3, PHOTOTRANSISTOR.pin3, DS3231.GND, LED_WARNING.cathode, LED_CRITICAL.cathode, DHT11_modul.pin3
  N8: ARDUINO_UNO.A4/SDA, LCD_16X2_I2C.SDA_-_I2C_Data, DS3231.SDA
  N9: ARDUINO_UNO.D0/RX, R4.Pin_0
  N10: ARDUINO_UNO.D1/TX, R3.Pin_0
  N11: ARDUINO_UNO.D7, DHT11_modul.pin2
  N12: ARDUINO_UNO.5V, R1.Pin_0, DHT11_modul.pin1
  N13: SMS.VCC, LCD_16X2_I2C.+V
  N14: WATERSNR.pin2, R2.Pin_0, DS3231.5V
  N15: LED_WARNING.anode, R4.Pin_1
  N16: LED_CRITICAL.anode, R3.Pin_1
